# Fritzing sketch Shema spajanja (saved by Fritzing 0.9.3b)
breadboards: 1

parts:
  Mod1 = Raspberry Pi Pico W
  Part1 = RFID-RC522-v2
  J1 = Piezo Speaker
  Keypad4x1 = Keypad Membran 4x4
  U1 = 7-SEGMENT-4DIGIT [package=7-segment-4digit-youngsun]
  Mod2 = Raspberry Pi Pico W
  J2 = Basic Servo
  HC-SR04_Sensor_1 = HC-SR04 Ultrasonic Distance Sensor

nets:
  N1: Mod1.pin_1, Keypad4x1.Pin5
  N2: Mod1.pin_2, Keypad4x1.Pin6
  N3: Mod1.pin_4, Keypad4x1.Pin7
  N4: Mod1.pin_5, Keypad4x1.Pin8
  N5: Mod1.pin_6, U1.16
  N6: Mod1.pin_7, U1.13
  N7: Mod1.pin_10, U1.8
  N8: Mod1.pin_11, U1.15
  N9: Mod1.pin_14, U1.6
  N10: Mod1.pin_15, U1.2
  N11: Mod1.pin_16, U1.1
  N12: Mod1.pin_17, U1.14
  N13: Mod1.pin_19, U1.11
  N14: Mod1.pin_20, U1.3
  N15: Mod1.pin_21, Part1.MISO
  N16: Mod1.pin_22, Part1.SDA
  N17: Mod1.pin_23, Mod1.pin_28, Mod1.pin_38, Mod1.pin_42, Part1.GND, J1.pin1, Keypad4x1.Pin2
  N18: Mod1.pin_24, Part1.SCK
  N19: Mod1.pin_25, Part1.MOSI
  N20: Mod1.pin_26, Part1.RST
  N21: Mod1.pin_27, Keypad4x1.Pin1
  N22: Mod1.pin_31, Keypad4x1.Pin3
  N23: Mod1.pin_32, Keypad4x1.Pin4
  N24: Mod1.pin_34, J1.pin2
  N25: Mod1.pin_39, Part1.3.3V
  GND: Mod2.pin_3, Mod2.pin_38, Mod2.pin_42, J2.gnd, HC-SR04_Sensor_1.GND
  N26: Mod2.pin_4, HC-SR04_Sensor_1.ECHO
  N27: Mod2.pin_5, HC-SR04_Sensor_1.TRIG
  N28: Mod2.pin_21, J2.pulse
  VCC: Mod2.pin_40, J2.vcc, HC-SR04_Sensor_1.VCC

custom parts:
  Raspberry Pi Pico W: Raspberry Pi Pico W. Based around the RP2040 microcontroller the Pico W is a low cost microcontroller device bringing Raspberry Pi quality, cost, and easy of use to the microcontroller space. The areas marked KEEPOUT in pcb silkscreen should not have traces running through them to avoid shorts on a soldered in module!
  RFID-RC522-v2: A simple China made RFID-RC522 Reader; do check the pin labels, as this is a MFRC522 based clone.
  Keypad Membran 4x4: Membrane Keypad 4x4 Matrix
